// Digital circuit nna1.dig as structural Verilog
module nna1 (
  input  clk,
  output [7:0] out_2,
  output [7:0] out_3,
  output [7:0] out_4,
  output [7:0] out_5
);

  wire add_1_c_o, and_1_out, and_3_out, and_4_out, and_5_out, and_6_out, and_11_out, and_12_out, and_13_out,
       and_14_out, c_prog, clf, dec, decoder_1_out_0, decoder_2_out_0, decoder_2_out_1, decoder_2_out_2,
       decoder_2_out_3, decoder_3_out_0, decoder_3_out_1, decoder_3_out_2, exec_2_nq, exec_2_q, flf, inc,
       jmp, not_1_out, not_2_out, not_3_out, not_4_out, not_5_out, not_6_out, not_7_out, not_8_out,
       not_9_out, notconnected_1_out, oflag_in, oflag_out, or_1_out, or_2_out, or_3_out, or_4_out, or_5_out,
       sub_1_c_o, t_ff_1_q, undriven;
  wire [1:0] arg0, arg1, reg_addr0;
  wire [7:0] add_1_s, PC_out, reg_in, reg_out0, reg_out1, sub_1_s;
  wire [7:4] rom_1_d;

  and and_1 (and_1_out, clk, exec_2_nq);
  T_FF t_ff_1 (.T(1'b1), .C(clk), .Q(t_ff_1_q));  // open: nQ
  or or_1 (or_1_out, c_prog, and_1_out);
  and and_2 (c_prog, t_ff_1_q, exec_2_q);
  LED exec (.in(exec_2_q));
  CounterPreset #(.Bits(8)) PC (
    .en(1'b1), .C(or_1_out), .dir(1'b0), .in({8{1'b0}}), .ld(1'b0), .clr(and_3_out), .out(PC_out));  // open: ovf
  and and_3 (and_3_out, exec_2_nq, and_4_out);
  RS_FF_AS exec_2 (.S(and_5_out), .R(1'b0), .Q(exec_2_q), .nQ(exec_2_nq));
  not not_1 (not_1_out, and_3_out);
  and and_4 (and_4_out, PC_out[0], PC_out[1], PC_out[2], PC_out[3]);
  and and_5 (and_5_out, ~t_ff_1_q, and_4_out);  // And
  and and_6 (and_6_out, not_1_out, exec_2_nq);
  ROM #(.AddrBits(8), .Bits(8)) rom_1 (.A(PC_out), .sel(exec_2_nq), .D({rom_1_d, arg0, arg1}));
  or or_2 (or_2_out, and_6_out, 1'b0);
  RAMSinglePortSel #(.AddrBits(8), .isProgramMemory("true"), .Bits(8)) main_mem (
    .A(PC_out), .CS(1'b1), .WE(or_2_out), .OE(1'b1), .D({rom_1_d, arg0, arg1}));
  Decoder #(.Selector_Bits(4)) decoder_1 (
    .sel(rom_1_d), .out_0(decoder_1_out_0));  // open: out_1, out_2, out_3, out_4, out_5, out_6, out_7, out_8, out_9, out_10, out_11, out_12, out_13, out_14, out_15
  Decoder #(.Selector_Bits(2)) decoder_2 (
    .sel(arg1), .out_0(decoder_2_out_0), .out_1(decoder_2_out_1), .out_2(decoder_2_out_2),
    .out_3(decoder_2_out_3));
  or or_3 (or_3_out, inc, dec);
  not not_2 (not_2_out, arg0[0]);
  Decoder #(.Selector_Bits(2)) decoder_3 (
    .sel(arg0), .out_0(decoder_3_out_0), .out_1(decoder_3_out_1), .out_2(decoder_3_out_2), .out_3(or_3_out));
  and and_7 (flf, decoder_1_out_0, not_2_out, arg0[1], decoder_2_out_0);
  and and_8 (jmp, decoder_2_out_1, decoder_1_out_0);
  and and_9 (inc, decoder_1_out_0, decoder_2_out_2);
  and and_10 (dec, decoder_1_out_0, decoder_2_out_3);
  and and_11 (and_11_out, undriven, decoder_3_out_0);
  and and_12 (and_12_out, undriven, decoder_3_out_1);
  and and_13 (and_13_out, undriven, decoder_3_out_2);
  and and_14 (and_14_out, undriven, or_3_out);
  and and_15 (clf, decoder_1_out_0, arg0[0], arg0[1], decoder_2_out_0);
  Register #(.Bits(8)) r0 (.D(reg_in), .C(c_prog), .en(and_11_out), .Q(out_2));
  Register #(.Bits(8)) r1 (.D(reg_in), .C(c_prog), .en(and_12_out), .Q(out_3));
  Register #(.Bits(8)) r2 (.D(reg_in), .C(c_prog), .en(and_13_out), .Q(out_4));
  Register #(.Bits(8)) r3 (.D(reg_in), .C(c_prog), .en(and_14_out), .Q(out_5));
  Multiplexer #(.Selector_Bits(2), .Bits(8)) multiplexer_1 (
    .sel(reg_addr0), .in_0(out_2), .in_1(out_3), .in_2(out_4), .in_3(out_5), .out(reg_out0));
  Multiplexer #(.Selector_Bits(2), .Bits(8)) multiplexer_2 (
    .sel(2'b00), .in_0(out_2), .in_1(out_3), .in_2(out_4), .in_3(out_5), .out(reg_out1));
  LED led_1 (.in(flf));
  LED led_2 (.in(clf));
  LED led_3 (.in(jmp));
  LED led_4 (.in(inc));
  LED led_5 (.in(dec));
  LED led_6 (.in(arg0[0]));
  LED led_7 (.in(arg0[1]));
  LED led_8 (.in(arg1[0]));
  LED led_9 (.in(arg1[1]));
  not not_3 (not_3_out, oflag_out);
  TransGate transgate_1 (.A(flf), .nA(not_4_out), .out1(not_3_out), .out2(oflag_in));
  TransGate transgate_2 (.A(clf), .nA(not_5_out), .out1(1'b0), .out2(oflag_in));
  not not_4 (not_4_out, flf);
  not not_5 (not_5_out, clf);
  or or_4 (or_4_out, inc, dec);
  TransGate #(.Bits(2)) transgate_3 (.A(or_4_out), .nA(notconnected_1_out), .out1(arg0), .out2(reg_addr0));
  // NotConnected on notconnected_1_out
  Add #(.Bits(8)) add_1 (.a(reg_out0), .b(8'h1), .c_i(oflag_out), .s(add_1_s), .c_o(add_1_c_o));
  Sub #(.Bits(8)) sub_1 (.a(reg_out0), .b(8'h1), .c_i(oflag_out), .s(sub_1_s), .c_o(sub_1_c_o));
  or or_5 (or_5_out, flf, clf, dec, inc);
  Register oflag (.D(oflag_in), .C(c_prog), .en(or_5_out), .Q(oflag_out));
  not not_6 (not_6_out, inc);
  TransGate #(.Bits(8)) transgate_4 (.A(inc), .nA(not_6_out), .out1(add_1_s), .out2(reg_in));
  not not_7 (not_7_out, inc);
  TransGate transgate_5 (.A(inc), .nA(not_7_out), .out1(add_1_c_o), .out2(oflag_in));
  not not_8 (not_8_out, dec);
  TransGate #(.Bits(8)) transgate_6 (.A(dec), .nA(not_8_out), .out1(sub_1_s), .out2(reg_in));
  not not_9 (not_9_out, dec);
  TransGate transgate_7 (.A(dec), .nA(not_9_out), .out1(sub_1_c_o), .out2(oflag_in));
  LED oflag_2 (.in(oflag_out));

  // Other names for the same wires on the sheet: clock = clk

  // Notes on the sheet:
  //   contents of rom_1 (hex, n*v repeats v):
  //   c,8,c,2,6,a,f,8
  //   op decoder
  //   opcode
  //   registers
  //   opcode = 0
  //   arg1
  //   arg0
  //   data in addr
  //   arg0 = 0
  //   write enable
  //   flf clf
  //   inc dec
  //   oflag
endmodule
