// Digital circuit nna8v0.dig as structural Verilog
module nna8v0 (
  input  C,
  input  RST,
  input  [7:0] A,
  input  [7:0] D,
  output R_W,
  output [1:0] brk
);

  wire add, add_1_c_o, add_2_c_o, \and , and_1_out, and_2_out, and_3_out, and_8_out, and_9_out, and_10_out,
       and_11_out, and_12_out, and_13_out, and_14_out, and_23_out, and_24_out, and_25_out, and_26_out,
       and_27_out, and_28_out, bra, clf, comparator_1_eq, comparator_1_lt, dec, decoder_1_out_0,
       decoder_1_out_1, decoder_1_out_2, decoder_1_out_3, decoder_2_out_0, decoder_3_out_0, decoder_3_out_1,
       decoder_3_out_2, decoder_3_out_3, eq, firstcycle, flf, gt, inc, jmp, lih, lil, mov, mrd, mul, mwr,
       nop, \not , not_1_out, not_2_out, not_3_out, not_4_out, not_5_out, not_6_out, not_7_out, not_8_out,
       not_9_out, not_10_out, not_12_out, not_13_out, not_14_out, not_15_out, not_16_out, not_17_out,
       not_18_out, not_19_out, not_20_out, not_21_out, not_22_out, oflag_out, \or , or_1_out, or_2_out,
       or_3_out, or_4_out, or_5_out, or_6_out, or_7_out, or_8_out, or_9_out, or_11_out, or_12_out, pc_write,
       rol, sub_1_c_o, \xor ;
  wire [1:0] and_5_out;
  wire [3:0] arg, curop_q;
  wire [7:0] add_1_s, add_2_s, and_22_out, barrelshifter_1_out, barrelshifter_2_out, not_11_out, or_10_out,
       pc, pc_next, r1_q, r2_q, r3_q, regin, regout_arg0, regout_arg1, regout_r0, sub_1_s, transgate_7_out2,
       xor_1_out;
  wire [15:0] mul_1_mul;

  CounterPreset #(.Bits(8), .isProgramCounter("true")) u_PC (
    .en(firstcycle), .C(C), .dir(1'b0), .in(pc_next), .ld(pc_write), .clr(RST), .out(pc));  // open: ovf
  or or_1 (or_1_out, mwr, mrd);
  or or_2 (or_2_out, bra, jmp);
  and and_1 (and_1_out, ~firstcycle, or_1_out);  // And
  and and_2 (and_2_out, ~firstcycle, mrd);  // And
  and and_3 (and_3_out, ~firstcycle, mwr);  // And
  or or_3 (or_3_out, brk[0], nop);
  or or_4 (or_4_out, lil, lih);
  not not_1 (not_1_out, jmp);
  TransGate #(.Bits(8)) transgate_1 (.A(firstcycle), .nA(not_2_out), .out1(pc), .out2(A));
  not not_2 (not_2_out, firstcycle);
  T_FF t_ff_1 (.T(1'b1), .C(C), .nQ(firstcycle));  // open: Q
  and and_4 (R_W, ~firstcycle, mwr);  // And
  or or_5 (or_5_out, mwr, bra, gt, eq, flf, clf, jmp, or_3_out);
  and and_5 (and_5_out[1], arg[3], ~or_4_out);  // And
  and and_6 (and_5_out[0], arg[2], ~or_4_out);  // And
  and and_7 (pc_write, or_2_out, ~oflag_out);  // And
  TransGate #(.Bits(8)) transgate_2 (.A(jmp), .nA(not_1_out), .out1(regout_arg0), .out2(pc_next));
  TransGate #(.Bits(8)) transgate_3 (.A(bra), .nA(not_3_out), .out1({pc[7:4], arg}), .out2(pc_next));
  not not_3 (not_3_out, bra);
  LED led_1 (.in(firstcycle));
  TransGate #(.Bits(8)) transgate_4 (.A(and_1_out), .nA(not_4_out), .out1(regout_arg1), .out2(A));
  not not_4 (not_4_out, and_1_out);
  TransGate #(.Bits(8)) transgate_5 (.A(and_2_out), .nA(not_5_out), .out1(D), .out2(regin));
  not not_5 (not_5_out, and_2_out);
  TransGate #(.Bits(8)) transgate_6 (.A(and_3_out), .nA(not_6_out), .out1(regout_arg0), .out2(D));
  not not_6 (not_6_out, and_3_out);
  and and_8 (and_8_out, ~or_5_out, ~firstcycle);  // And
  Decoder #(.Selector_Bits(2)) decoder_1 (
    .sel(and_5_out), .out_0(decoder_1_out_0), .out_1(decoder_1_out_1), .out_2(decoder_1_out_2),
    .out_3(decoder_1_out_3));
  TransGate #(.Bits(8)) transgate_7 (.A(not_7_out), .nA(RST), .out1(regin), .out2(transgate_7_out2));
  and and_9 (and_9_out, and_8_out, decoder_1_out_0);
  and and_10 (and_10_out, and_8_out, decoder_1_out_1);
  and and_11 (and_11_out, and_8_out, decoder_1_out_2);
  and and_12 (and_12_out, and_8_out, decoder_1_out_3);
  Decoder #(.Selector_Bits(4)) decoder_2 (
    .sel(curop_q), .out_0(decoder_2_out_0), .out_1(lil), .out_2(lih), .out_3(mwr), .out_4(mrd), .out_5(mov),
    .out_6(bra), .out_7(rol), .out_8(eq), .out_9(gt), .out_10(add), .out_11(mul), .out_12(\and ),
    .out_13(\not ), .out_14(\or ), .out_15(\xor ));
  Register #(.Bits(8)) curop (.D(D), .C(C), .en(firstcycle), .Q({curop_q, arg}));
  not not_7 (not_7_out, RST);
  or or_6 (or_6_out, and_9_out, RST);
  or or_7 (or_7_out, and_10_out, RST);
  or or_8 (or_8_out, and_11_out, RST);
  or or_9 (or_9_out, and_12_out, RST);
  Decoder #(.Selector_Bits(2)) decoder_3 (
    .sel(arg[1:0]), .out_0(decoder_3_out_0), .out_1(decoder_3_out_1), .out_2(decoder_3_out_2),
    .out_3(decoder_3_out_3));
  and and_13 (and_13_out, ~arg[2], ~arg[3]);  // And
  and and_14 (and_14_out, arg[2], ~arg[3]);  // And
  LED led_2 (.in(arg[2]));
  LED led_3 (.in(arg[3]));
  LED led_4 (.in(arg[0]));
  LED led_5 (.in(arg[1]));
  PullDown #(.Bits(8)) pulldown_1 (.out(transgate_7_out2));
  Register #(.Bits(8)) r0 (.D(transgate_7_out2), .C(C), .en(or_6_out), .Q(regout_r0));
  Register #(.Bits(8)) r1 (.D(transgate_7_out2), .C(C), .en(or_7_out), .Q(r1_q));
  Register #(.Bits(8)) r2 (.D(transgate_7_out2), .C(C), .en(or_8_out), .Q(r2_q));
  Register #(.Bits(8)) r3 (.D(transgate_7_out2), .C(C), .en(or_9_out), .Q(r3_q));
  not not_8 (not_8_out, arg[2]);
  and and_15 (nop, and_13_out, decoder_3_out_0, decoder_2_out_0);
  and and_16 (brk[0], and_14_out, decoder_3_out_0, decoder_2_out_0);
  Break #(.Cycles(1000000)) u_brk (.brk(brk[0]));
  and and_17 (jmp, decoder_3_out_1, decoder_2_out_0);
  and and_18 (inc, decoder_2_out_0, decoder_3_out_2);
  and and_19 (dec, decoder_2_out_0, decoder_3_out_3);
  and and_20 (flf, decoder_2_out_0, decoder_3_out_0, not_8_out, arg[3]);
  and and_21 (clf, decoder_2_out_0, decoder_3_out_0, arg[2], arg[3]);
  Multiplexer #(.Selector_Bits(2), .Bits(8)) multiplexer_1 (
    .sel(arg[3:2]), .in_0(regout_r0), .in_1(r1_q), .in_2(r2_q), .in_3(r3_q), .out(regout_arg0));
  Multiplexer #(.Selector_Bits(2), .Bits(8)) multiplexer_2 (
    .sel(arg[1:0]), .in_0(regout_r0), .in_1(r1_q), .in_2(r2_q), .in_3(r3_q), .out(regout_arg1));
  LED led_6 (.in(nop));
  LED led_7 (.in(brk[0]));
  LED led_8 (.in(flf));
  LED led_9 (.in(clf));
  LED led_10 (.in(jmp));
  LED led_11 (.in(inc));
  LED led_12 (.in(dec));
  LED led_13 (.in(lil));
  LED led_14 (.in(lih));
  LED led_15 (.in(mwr));
  LED led_16 (.in(mrd));
  LED led_17 (.in(mov));
  LED led_18 (.in(bra));
  LED led_19 (.in(rol));
  LED led_20 (.in(eq));
  LED led_21 (.in(gt));
  LED led_22 (.in(add));
  LED led_23 (.in(mul));
  LED led_24 (.in(\and ));
  LED led_25 (.in(\not ));
  LED led_26 (.in(\or ));
  LED led_27 (.in(\xor ));
  not not_9 (not_9_out, oflag_out);
  not not_10 (not_10_out, mov);
  TransGate #(.Bits(8)) transgate_8 (.A(mov), .nA(not_10_out), .out1(regout_arg1), .out2(regin));
  Add #(.Bits(8)) add_1 (.a(regout_arg0), .b(8'h1), .c_i(oflag_out), .s(add_1_s), .c_o(add_1_c_o));
  Sub #(.Bits(8)) sub_1 (.a(regout_arg0), .b(8'h1), .c_i(oflag_out), .s(sub_1_s), .c_o(sub_1_c_o));
  assign and_22_out = regout_arg0 & regout_arg1;  // And and_22, 8 bits wide
  assign not_11_out = ~regout_arg1;  // Not not_11, 8 bits wide
  assign or_10_out = regout_arg0 | regout_arg1;  // Or or_10, 8 bits wide
  assign xor_1_out = regout_arg0 ^ regout_arg1;  // XOr xor_1, 8 bits wide
  TransGate #(.Bits(8)) transgate_9 (.A(lil), .nA(not_12_out), .out1({regout_r0[7:4], arg}), .out2(regin));
  not not_12 (not_12_out, lil);
  TransGate #(.Bits(8)) transgate_10 (.A(lih), .nA(not_13_out), .out1({arg, regout_r0[3:0]}), .out2(regin));
  not not_13 (not_13_out, lih);
  and and_23 (and_23_out, flf, not_9_out);
  TransGate #(.Bits(8)) transgate_11 (.A(inc), .nA(not_14_out), .out1(add_1_s), .out2(regin));
  and and_24 (and_24_out, add_1_c_o, inc);
  TransGate #(.Bits(8)) transgate_12 (.A(dec), .nA(not_15_out), .out1(sub_1_s), .out2(regin));
  and and_25 (and_25_out, sub_1_c_o, dec);
  TransGate #(.Bits(8)) transgate_13 (.A(\and ), .nA(not_16_out), .out1(and_22_out), .out2(regin));
  TransGate #(.Bits(8)) transgate_14 (.A(\not ), .nA(not_17_out), .out1(not_11_out), .out2(regin));
  TransGate #(.Bits(8)) transgate_15 (.A(\or ), .nA(not_18_out), .out1(or_10_out), .out2(regin));
  TransGate #(.Bits(8)) transgate_16 (.A(\xor ), .nA(not_19_out), .out1(xor_1_out), .out2(regin));
  not not_14 (not_14_out, inc);
  not not_15 (not_15_out, dec);
  not not_16 (not_16_out, \and );
  not not_17 (not_17_out, \not );
  not not_18 (not_18_out, \or );
  not not_19 (not_19_out, \xor );
  Comparator #(.Bits(8)) comparator_1 (
    .a(regout_arg0), .b(regout_arg1), .eq(comparator_1_eq), .lt(comparator_1_lt));  // open: gt
  Add #(.Bits(8)) add_2 (.a(regout_arg0), .b(regout_arg1), .c_i(oflag_out), .s(add_2_s), .c_o(add_2_c_o));
  Mul #(.Bits(8)) mul_1 (.a(regout_arg0), .b(regout_arg1), .mul(mul_1_mul));
  BarrelShifter #(.Bits(8), .barrelShifterMode("rotate")) barrelshifter_1 (
    .in(regout_arg0), .shift(regout_arg1[3:0]), .out(barrelshifter_1_out));
  TransGate #(.Bits(8)) transgate_17 (.A(add), .nA(not_20_out), .out1(add_2_s), .out2(regin));
  and and_26 (and_26_out, add_2_c_o, add);
  BarrelShifter #(.Bits(8), .barrelShifterMode("rotate")) barrelshifter_2 (
    .in(barrelshifter_1_out), .shift(regout_arg1[7:4]), .out(barrelshifter_2_out));
  and and_27 (and_27_out, eq, ~comparator_1_eq);  // And
  and and_28 (and_28_out, ~comparator_1_lt, gt);  // And
  not not_20 (not_20_out, add);
  not not_21 (not_21_out, mul);
  TransGate #(.Bits(8)) transgate_18 (.A(mul), .nA(not_21_out), .out1(mul_1_mul[7:0]), .out2(regin));
  not not_22 (not_22_out, rol);
  TransGate #(.Bits(8)) transgate_19 (.A(rol), .nA(not_22_out), .out1(barrelshifter_2_out), .out2(regin));
  or or_11 (or_11_out, and_23_out, and_24_out, and_25_out, and_27_out, and_28_out, and_26_out);
  or or_12 (or_12_out, flf, clf, eq, gt, dec, inc);
  Register oflag (.D(or_11_out), .C(C), .en(or_12_out), .Q(oflag_out));
  LED oflag_2 (.in(oflag_out));
  // Pins of 1 and 2 bits meet at brk
  // Pins of 1 and 8 bits meet at A
  // Pins of 1 and 8 bits meet at D

  // Other names for the same wires on the sheet: arg1[1:0] = arg[1:0]; arg0[1:0] = arg[3:2]; addrbus[7:0] = A;
  //   clock = C; mbus[7:0] = D; reset = RST

  // Notes on the sheet:
  //   R_W: Indicates that the processor wants to write or read from the address on the address bus
  //   High: Write
  //   Low: Read, pin 1
  //   C: clock signal, pin 1
  //   RST: resets the processor on the next clock cycle, pin 4
  //   A: address bus, pin 2
  //   D: data bus, pin 3
  //   brk: high when the brk instruction is executing, pin 1
  //   pc,clock
  //   io
  //   mwr, mrd
  //   registers
  //   jmp bra
  //   select r0 on lil,lih ops
  //   regin_addr
  //   op decoder
  //   write enable
  //   opcode = 0
  //   opcode
  //   arg1 = 0
  //   lil lih
  //   flf clf mov
  //   alu
  //   oflag
endmodule
