// Digital circuit bit-eater-v2.dig as structural Verilog
module bit_eater_v2 (
  input  clk
);

  wire add_2_c_o, and_1_out, and_9_out, and_10_out, and_11_out, and_12_out, and_13_out, and_14_out,
       and_18_out, and_19_out, and_20_out, and_22_out, and_23_out, and_24_out, bra, brk, cal, cal_flag,
       comparator_1_eq, comparator_1_lt, d_ff_1_nq, dec, dec_flag, decoder_1_out_0, decoder_1_out_1,
       decoder_2_out_0, decoder_2_out_1, decoder_2_out_2, decoder_2_out_3, decoder_4_out_0, decoder_4_out_1,
       decoder_4_out_2, decoder_4_out_3, decoder_5_out_0, decoder_5_out_1, decoder_5_out_2, decoder_6_out_0,
       decoder_6_out_1, decoder_6_out_2, decoder_6_out_3, dread, dwrite, dwrite_video, eq, eq_flag, flg,
       flg_flag, gt, gt_flag, inc, inc_flag, jmp, lih, lil, mco, mdb, mov, mpb, mrd, multiplexer_3_out, mwr,
       nclock, nop, not_3_out, not_4_out, not_5_out, not_6_out, not_7_out, not_9_out, not_10_out, oflag_out,
       or_1_out, or_2_out, or_4_out, or_5_out, or_6_out, pc_write, sin, sub_2_c_o, xcycle, xcycle_next, \xor ;
  wire [1:0] and_7_out;
  wire [3:0] arg, co, curop;
  wire [7:0] add_1_s, add_2_s, addrbus, d_ff_as_1_q, d_ff_as_2_q, d_ff_as_3_q, d_ff_as_4_q, databus, db,
       driver_9_out, driver_15_out, pb, pc, pc_next, r1_q, r2_q, r3_q, regin, regout_arg0, regout_arg1,
       regout_r0, sub_1_s, sub_2_s, video_addr, video_data;
  wire [15:0] mul_1_mul;
  wire [15:8] addrbus_full;

  Decoder #(.Selector_Bits(2)) decoder_1 (
    .sel(arg[3:2]), .out_0(decoder_1_out_0), .out_1(decoder_1_out_1));  // open: out_2, out_3
  Decoder #(.Selector_Bits(2)) decoder_2 (
    .sel(arg[1:0]), .out_0(decoder_2_out_0), .out_1(decoder_2_out_1), .out_2(decoder_2_out_2),
    .out_3(decoder_2_out_3));
  and and_1 (and_1_out, sin, decoder_2_out_0);
  // Probe on arg[3:2]
  // Probe on arg[1:0]
  Register #(.Bits(8)) u_curop (.D(databus), .C(clk), .en(~xcycle), .Q({curop, arg}));
  or or_1 (or_1_out, lil, lih);
  and and_2 (nop, and_1_out, decoder_1_out_0);
  and and_3 (brk, and_1_out, decoder_1_out_1);
  and and_4 (jmp, decoder_2_out_1, sin);
  and and_5 (mpb, decoder_2_out_2, sin);
  and and_6 (mdb, decoder_2_out_3, sin);
  Decoder #(.Selector_Bits(4)) decoder_3 (
    .sel(curop), .out_0(sin), .out_1(eq), .out_2(gt), .out_3(flg), .out_5(bra), .out_6(mco), .out_7(mwr),
    .out_8(mrd), .out_9(lil), .out_10(lih), .out_11(mov), .out_12(cal), .out_13(\xor ), .out_14(inc),
    .out_15(dec));  // open: out_4
  // Probe on curop
  // Probe on arg
  and and_7 (and_7_out[1], arg[3], ~or_1_out);  // And
  and and_8 (and_7_out[0], arg[2], ~or_1_out);  // And
  Decoder #(.Selector_Bits(2)) decoder_4 (
    .sel(and_7_out), .out_0(decoder_4_out_0), .out_1(decoder_4_out_1), .out_2(decoder_4_out_2),
    .out_3(decoder_4_out_3));
  assign regin = mov ? regout_arg1 : 8'bz;  // Driver driver_1
  and and_9 (and_9_out, decoder_4_out_0, curop[3]);
  and and_10 (and_10_out, decoder_4_out_1, curop[3]);
  and and_11 (and_11_out, decoder_4_out_2, curop[3]);
  and and_12 (and_12_out, decoder_4_out_3, curop[3]);
  assign regin = lil ? {regout_r0[7:4], arg} : 8'bz;  // Driver driver_2
  assign regin = lih ? {arg, regout_r0[3:0]} : 8'bz;  // Driver driver_3
  Comparator #(.Bits(8)) comparator_1 (
    .a(regout_arg0), .b(regout_arg1), .eq(comparator_1_eq), .lt(comparator_1_lt));  // open: gt
  Add #(.Bits(8)) add_1 (.a(regout_arg0), .b({{6{1'b0}}, arg[1:0]}), .c_i(1'b1), .s(add_1_s), .c_o(inc_flag));
  Sub #(.Bits(8)) sub_1 (.a(regout_arg0), .b({{6{1'b0}}, arg[1:0]}), .c_i(1'b1), .s(sub_1_s), .c_o(dec_flag));
  not not_1 (eq_flag, comparator_1_eq);
  not not_2 (gt_flag, comparator_1_lt);
  PullDown #(.Bits(8)) pulldown_1 (.out(regin));
  Register #(.Bits(8)) r0 (.D(regin), .C(nclock), .en(and_9_out), .Q(regout_r0));
  Register #(.Bits(8)) r1 (.D(regin), .C(nclock), .en(and_10_out), .Q(r1_q));
  Register #(.Bits(8)) r2 (.D(regin), .C(nclock), .en(and_11_out), .Q(r2_q));
  Register #(.Bits(8)) r3 (.D(regin), .C(nclock), .en(and_12_out), .Q(r3_q));
  Register #(.Bits(8)) u_pb (.D(regout_arg0), .C(nclock), .en(mpb), .Q(pb));
  Register #(.Bits(8)) u_db (.D(regout_arg0), .C(nclock), .en(mdb), .Q(db));
  Register #(.Bits(4)) u_co (.D(arg), .C(nclock), .en(mco), .Q(co));
  assign regin = inc ? add_1_s : 8'bz;  // Driver driver_4
  assign regin = dec ? sub_1_s : 8'bz;  // Driver driver_5
  // Probe on regout_r0
  // Probe on r1_q
  // Probe on r2_q
  // Probe on r3_q
  // Probe on pb
  // Probe on db
  // Probe on co
  not not_3 (not_3_out, oflag_out);
  not not_4 (not_4_out, arg[2]);
  Decoder #(.Selector_Bits(4)) decoder_5 (
    .sel(co), .out_0(decoder_5_out_0), .out_1(decoder_5_out_1), .out_2(decoder_5_out_2));  // open: out_3, out_4, out_5, out_6, out_7, out_8, out_9, out_10, out_11, out_12, out_13, out_14, out_15
  CounterPreset #(.Bits(8), .isProgramCounter("true")) u_PC (
    .en(~xcycle), .C(clk), .dir(1'b0), .in(pc_next), .ld(pc_write), .clr(mpb), .out(pc));  // open: ovf
  and and_13 (and_13_out, not_3_out, not_4_out);
  and and_14 (and_14_out, arg[3], arg[2]);
  Multiplexer #(.Selector_Bits(2), .Bits(8)) multiplexer_1 (
    .sel(arg[3:2]), .in_0(regout_r0), .in_1(r1_q), .in_2(r2_q), .in_3(r3_q), .out(regout_arg0));
  Multiplexer #(.Selector_Bits(2), .Bits(8)) multiplexer_2 (
    .sel(arg[1:0]), .in_0(regout_r0), .in_1(r1_q), .in_2(r2_q), .in_3(r3_q), .out(regout_arg1));
  not not_5 (not_5_out, xcycle);
  or or_2 (or_2_out, mrd, pc_write, mwr);
  or or_3 (flg_flag, and_13_out, and_14_out);
  assign addrbus = not_5_out ? pc : 8'bz;  // Driver driver_6
  and and_15 (xcycle_next, d_ff_1_nq, or_2_out);
  // Probe on databus
  // Probe on addrbus
  and and_16 (dwrite, xcycle, mwr);
  and and_17 (dread, xcycle, mrd);
  or or_4 (or_4_out, dwrite, dread);
  assign addrbus_full = or_4_out ? db : 8'bz;  // Driver driver_7
  assign addrbus_full = not_6_out ? pb : 8'bz;  // Driver driver_8
  D_FF d_ff_1 (.D(xcycle_next), .C(~clk), .Q(xcycle), .nQ(d_ff_1_nq));
  Add #(.Bits(8)) add_2 (.a(regout_arg0), .b(regout_arg1), .c_i(oflag_out), .s(add_2_s), .c_o(add_2_c_o));
  Sub #(.Bits(8)) sub_2 (.a(regout_arg0), .b(regout_arg1), .c_i(oflag_out), .s(sub_2_s), .c_o(sub_2_c_o));
  Mul #(.Bits(8)) mul_1 (.a(regout_arg0), .b(regout_arg1), .mul(mul_1_mul));
  not not_6 (not_6_out, or_4_out);
  not not_7 (not_7_out, addrbus_full[8]);
  // Probe on pc
  // Probe on addrbus
  // Probe on databus
  // Probe on xcycle
  Break u_brk (.brk(brk));
  LED led_1 (.in(xcycle));
  assign driver_9_out = decoder_5_out_0 ? add_2_s : 8'bz;  // Driver driver_9
  assign driver_9_out = decoder_5_out_1 ? sub_2_s : 8'bz;  // Driver driver_10
  assign driver_9_out = decoder_5_out_2 ? mul_1_mul[7:0] : 8'bz;  // Driver driver_11
  or or_5 (or_5_out, mwr, mrd);
  and and_18 (and_18_out, clk, dwrite);
  and and_19 (and_19_out, not_7_out, addrbus_full[9], addrbus_full[10], addrbus_full[11], addrbus_full[12], addrbus_full[13], addrbus_full[14], addrbus_full[15]);
  not not_8 (nclock, clk);
  Multiplexer #(.Selector_Bits(4)) multiplexer_3 (
    .sel(curop), .in_0(oflag_out), .in_1(eq_flag), .in_2(gt_flag), .in_3(flg_flag), .in_4(oflag_out),
    .in_5(oflag_out), .in_6(oflag_out), .in_7(oflag_out), .in_8(oflag_out), .in_9(oflag_out),
    .in_10(oflag_out), .in_11(oflag_out), .in_12(cal_flag), .in_13(oflag_out), .in_14(inc_flag),
    .in_15(dec_flag), .out(multiplexer_3_out));
  assign regin = cal ? driver_9_out : 8'bz;  // Driver driver_12
  and and_20 (and_20_out, xcycle, or_5_out);
  or or_6 (or_6_out, addrbus_full[12], addrbus_full[13], addrbus_full[14], addrbus_full[15]);
  assign regin = dread ? databus : 8'bz;  // Driver driver_13
  assign databus = dwrite ? regout_arg0 : 8'bz;  // Driver driver_14
  and and_21 (dwrite_video, and_19_out, dwrite);
  assign driver_15_out = dwrite_video ? addrbus : 8'bz;  // Driver driver_15
  assign driver_15_out = ~dwrite_video ? video_addr : 8'bz;  // DriverInvSel driverinvsel_1
  not not_9 (not_9_out, clk);
  assign addrbus = and_20_out ? regout_arg1 : 8'bz;  // Driver driver_16
  EEPROM #(.AddrBits(13), .isProgramMemory("true"), .Bits(8)) eeprom_1 (
    .A({1'b0, addrbus_full[11:8], addrbus}), .CS(~or_6_out), .WE(and_18_out), .OE(~dwrite), .D(databus));
  and and_22 (and_22_out, bra, ~oflag_out);  // And
  Register flag (.D(multiplexer_3_out), .C(not_9_out), .en(1'b1), .Q(oflag_out));
  Multiplexer #(.Selector_Bits(4)) multiplexer_4 (
    .sel(co), .in_0(add_2_c_o), .in_1(sub_2_c_o), .in_2(oflag_out), .in_3(1'b0), .in_4(1'b0), .in_5(1'b0),
    .in_6(1'b0), .in_7(1'b0), .in_8(1'b0), .in_9(1'b0), .in_10(1'b0), .in_11(1'b0), .in_12(1'b0),
    .in_13(1'b0), .in_14(1'b0), .in_15(1'b0), .out(cal_flag));
  and and_23 (and_23_out, clk, dwrite_video);
  and and_24 (and_24_out, jmp, ~oflag_out);  // And
  not not_10 (not_10_out, dwrite_video);
  assign pc_next = and_22_out ? {pc[7:4], arg} : 8'bz;  // Driver driver_17
  assign pc_next = and_24_out ? regout_arg0 : 8'bz;  // Driver driver_18
  RAMSinglePortSel #(.AddrBits(15), .Bits(8)) ramsingleportsel_1 (
    .A({{7{1'b0}}, driver_15_out}), .CS(1'b1), .WE(and_23_out), .OE(not_10_out), .D(video_data));
  or or_7 (pc_write, and_22_out, and_24_out);
  CounterPreset #(.Bits(8), .isProgramCounter("true")) counterpreset_1 (
    .en(~dwrite_video), .C(clk), .dir(1'b0), .in({8{1'b0}}), .ld(1'b0), .clr(1'b0), .out(video_addr));  // open: ovf
  assign video_data = dwrite_video ? databus : 8'bz;  // Driver driver_19
  Decoder #(.Selector_Bits(2)) decoder_6 (
    .sel(video_addr[1:0]), .out_0(decoder_6_out_0), .out_1(decoder_6_out_1), .out_2(decoder_6_out_2),
    .out_3(decoder_6_out_3));
  D_FF_AS #(.Bits(8)) d_ff_as_1 (
    .Set(1'b0), .D(video_data), .C(~decoder_6_out_3), .Clr(decoder_6_out_0), .Q(d_ff_as_1_q));  // open: nQ
  D_FF_AS #(.Bits(8)) d_ff_as_2 (
    .Set(1'b0), .D(video_data), .C(~decoder_6_out_2), .Clr(decoder_6_out_0), .Q(d_ff_as_2_q));  // open: nQ
  D_FF_AS #(.Bits(8)) d_ff_as_3 (
    .Set(1'b0), .D(video_data), .C(~decoder_6_out_1), .Clr(decoder_6_out_0), .Q(d_ff_as_3_q));  // open: nQ
  D_FF_AS #(.Bits(8)) d_ff_as_4 (
    .Set(1'b0), .D(video_data), .C(~decoder_6_out_0), .Clr(1'b0), .Q(d_ff_as_4_q));  // open: nQ
  LedMatrix #(.ledPersistence("true"), .colAddrBits(6), .rowDataBits(32)) display (
    .rows({d_ff_as_4_q, d_ff_as_3_q, d_ff_as_2_q, d_ff_as_1_q}), .column(video_addr[7:2]));

  // Other names for the same wires on the sheet: arg1[1:0] = arg[1:0]; arg0[1:0] = arg[3:2]; reg_we = curop[3];
  //   addrbus_full[7:0] = addrbus; clock = clk

  // Notes on the sheet:
  //   clk: Hz: 100
  //   sin
  //   op decoder
  //   registers
  //   select r0 on lil,lih ops
  //   lil lih
  //   mov
  //   regin_addr
  //   alu
  //   flg
  //   pc,clock
  //   mwr, mrd
  //   main mem
  //   video mem
  //   flag
  //   jmp bra
  //   contents of eeprom_1 (hex, n*v repeats v):
  //   da,9f,a0,1,4,34,54,8*0,91,a0,3,8c,94,68,c8,4,92,3,86,f3,3,77,e8
  //   ,ef,57,91,3,7c,4,476*0,fe,9,9,fe,fe,9,9,fe
  //   video display
endmodule
